# Fritzing sketch Diagram (saved by Fritzing 0.8.5b)
breadboards: 1

parts:
  Part1 = Arduino Nano (Rev3.0)
  Part3 = Adafruit FONA - Mini Cellular GSM Breakout

nets:
  GND: Part1.GND, Part3.PWRKEY_5V, Part3.GND
  N1: Part1.VIN, Part3.VCCIO, Part3.VBAT

custom parts:
  Adafruit FONA - Mini Cellular GSM Breakout: An all-in-one cellular phone module that lets you add voice, text, SMS and GPRS data to your project. Quad-band 850/900/1800/1900MHz - connect onto any global GSM network with any 2G SIM. Includes an onboard LiPoly battery charging circuitry so you can take your project on the go. Also works as an FM radio receiver.
